# Fritzing sketch 2020_10_04_patio_motherboard (saved by Fritzing 0.9.4)
perfboards: 4

parts:
  J2 = female pin header, 5 pins [form="♀ (female)"]  # not connected
  J3 = female pin header, 20 pins [form="♀ (female)"]
  J4 = female pin header, 20 pins [form="♀ (female)"]
  J1 = female pin header, 30 pins [form="♀ (female)"]
  J7 = female pin header, 1 pin [form="♀ (female)"]  # not connected
  J8 = female pin header, 1 pin [form="♀ (female)"]
  R2 = Resistor [tolerance=±5% resistance=220 package=THT]  # not connected
  LED2 = LED - 3mm [color="Green (560nm)" package="3 mm [THT]"]  # not connected
  J9 = female pin header, 17 pins [form="♀ (female)"]
  J10 = female pin header, 13 pins [form="♀ (female)"]
  J12 = female pin header, 13 pins [form="♀ (female)"]
  J13 = female pin header, 4 pins [form="♀ (female)"]  # not connected
  J14 = female pin header, 13 pins [form="♀ (female)"]
  J16 = female pin header, 2 pins [form="♀ (female)"]
  R3 = Resistor [tolerance=±5% resistance=220 package=THT]  # not connected
  J15 = female pin header, 4 pins [form="♀ (female)"]
  R4 = Resistor [tolerance=±5% resistance=220 package=THT]  # not connected
  J18 = female pin header, 8 pins [form="♀ (female)"]
  R14 = Resistor [tolerance=±5% resistance=220 package=THT]
  R15 = Resistor [tolerance=±5% resistance=220 package=THT]
  J19 = female pin header, 4 pins [form="♀ (female)"]
  J20 = female pin header, 30 pins [form="♀ (female)"]
  F2 = FUSE [package=fuse_5mm]  # not connected
  J21 = female pin header, 8 pins [form="♀ (female)"]
  J22 = female pin header, 8 pins [form="♀ (female)"]
  J23 = female pin header, 8 pins [form="♀ (female)"]
  J24 = female pin header, 8 pins [form="♀ (female)"]
  J25 = female pin header, 8 pins [form="♀ (female)"]
  J26 = female pin header, 8 pins [form="♀ (female)"]
  J27 = female pin header, 8 pins [form="♀ (female)"]
  J28 = female pin header, 8 pins [form="♀ (female)"]
  J29 = female pin header, 8 pins [form="♀ (female)"]
  J30 = female pin header, 8 pins [form="♀ (female)"]
  J31 = female pin header, 8 pins [form="♀ (female)"]
  J32 = female pin header, 8 pins [form="♀ (female)"]
  J33 = female pin header, 13 pins [form="♀ (female)"]  # not connected

nets:
  N1: J3.pin2, J1.pin28, J9.pin15, J10.pin5
  N2: J3.pin3, J10.pin6
  N3: J3.pin4, J10.pin7
  N4: J3.pin5, J10.pin8
  N5: J3.pin6, J10.pin9
  N6: J3.pin8, J10.pin11
  N7: J3.pin9, J10.pin12
  N8: J3.pin11, J10.pin13
  N9: J3.pin12, J9.pin1
  N10: J3.pin13, J9.pin2
  N11: J3.pin16, J9.pin3
  N12: J3.pin17, J9.pin4
  N13: J3.pin18, J9.pin5
  N14: J3.pin19, J9.pin6
  N15: J3.pin20, J9.pin7
  N16: J4.pin1, J1.pin1, J10.pin4
  N17: J4.pin2, J1.pin2
  N18: J4.pin3, J1.pin3
  N19: J4.pin4, J1.pin4, J10.pin2
  N20: J4.pin5, J1.pin5, J1.pin30, J9.pin17, J12.pin3
  N21: J4.pin6, J1.pin6
  N22: J4.pin7, J1.pin7
  N23: J4.pin8, J1.pin8
  N24: J4.pin9, J1.pin9, J1.pin27, J9.pin14
  N25: J4.pin10, J1.pin10
  N26: J4.pin11, J1.pin11
  N27: J4.pin12, J1.pin12
  N28: J4.pin13, J1.pin13
  N29: J4.pin14, J1.pin14
  N30: J4.pin15, J1.pin15
  N31: J4.pin16, J1.pin16
  N32: J4.pin17, J1.pin17
  N33: J4.pin18, J1.pin18
  N34: J4.pin19, J1.pin19
  N35: J4.pin20, J1.pin20
  N36: J1.pin24, J9.pin11
  N37: J1.pin25, J9.pin12
  N38: J1.pin26, J9.pin13
  N39: J1.pin29, J8.pin1
  N40: J10.pin1, J12.pin1
  N41: J10.pin10, J12.pin10
  N42: J14.pin4, J16.pin2
  N43: J14.pin6, J15.pin1
  N44: J14.pin11, J15.pin3
  N45: J14.pin13, J16.pin1
  N46: J18.pin1, J24.pin1, J32.pin5
  N47: J18.pin2, J24.pin2, J32.pin6
  N48: J18.pin3, J24.pin3
  N49: J18.pin4, J24.pin4, J25.pin6
  N50: J18.pin5, J24.pin5
  N51: J18.pin6, J24.pin6
  N52: J18.pin7, J24.pin7
  N53: J18.pin8, J24.pin8, J25.pin3, J25.pin5
  N54: R14.Pin_0, J19.pin4
  N55: R15.Pin_1, J19.pin1
  N56: J20.pin30, J21.pin6, J32.pin1
  N57: J21.pin1, J28.pin5
  N58: J21.pin2, J28.pin6
  N59: J21.pin4, J27.pin6
  N60: J21.pin8, J27.pin3, J27.pin5
  N61: J22.pin1, J29.pin5
  N62: J22.pin2, J29.pin6
  N63: J22.pin4, J26.pin6
  N64: J22.pin8, J26.pin3, J26.pin5
  N65: J23.pin1, J31.pin5
  N66: J23.pin2, J31.pin6
  N67: J23.pin4, J30.pin6
  N68: J23.pin8, J30.pin3, J30.pin5
  N69: J25.pin1, J25.pin4
  N70: J26.pin1, J26.pin4
  N71: J27.pin1, J27.pin2, J27.pin4, J32.pin2
  N72: J30.pin1, J30.pin4

notes:
  +5V
  GND
  GPIO 03
  GPIO 17
  GPIO14
  +12V
  +3V
  GPIO 02
  GPIO 22
  GPIO 10
  GPIO 11
  GPIO 5
  GPIO 19
  GPIO 26
  GPIO 27
  GPIO 9
  ID_SD
  GPIO 6
  GPIO 13
  GPIO15
  GPIO18
  GPIO24
  GPIO8
  GPIO7
  GPIO12
  GPIO16
  GPIO20
  GPIO21
  GPIO 04
  GPIO 23
  GPIO 25
  driver in
  +3V/Null
  swicht manual
  DGO-3512ADA
  motor ctrl 2
  motor crtl 3
  motor ctrl 4
  out2 (+12V or GND)
  out1 (+12V or GND)
  Traco power TSR 1-2450
  ...
  Pin 2: GND
  Pin 1: 12V
  Pin 3: 5 V
  motor ctrl 1
